# Fritzing sketch RFID collector - (Buscheck) (saved by Fritzing 1.0.1rc)
breadboards: 1

parts:
  Componente1 = RFID-RC522-v3
  Mod2 = Passive Buzzer
  YwRobot_Power_Supply1 = YwRobot Breadboard Power Supply [part_number=545043]
  U1 = NodeMCU V1.0
  LED1 = smd LED [color="Red (633nm)" package="0805 [SMD]"]
  LED2 = smd LED [color="Yellow (595nm)" current=0A package="0805 [SMD]"]
  R1 = Resistor [tolerance=±5% resistance=220 package="2010 [SMD]"]
  R2 = Resistor [tolerance=±5% resistance=220 package="2010 [SMD]"]

nets:
  N1: Componente1.SDA, U1.D8
  N2: Componente1.SCK, U1.D5
  N3: Componente1.MOSI, U1.D7
  N4: Componente1.MISO, U1.D6
  GND: Componente1.GND, Mod2.-, YwRobot_Power_Supply1.GND#11, YwRobot_Power_Supply1.GND#12, U1.GND, LED1.cathode, LED2.cathode
  N5: Componente1.RST, U1.D0
  3.3V: Componente1.3.3V, U1.3V3
  N6: Mod2.S, YwRobot_Power_Supply1.VCC#5, YwRobot_Power_Supply1.VCC#6, U1.Vin
  N7: Mod2.NC, U1.D4
  N8: YwRobot_Power_Supply1.VCC#9, YwRobot_Power_Supply1.VCC#10
  N9: YwRobot_Power_Supply1.GND#13, YwRobot_Power_Supply1.GND#14
  N10: U1.D2, R2.Pin_0
  N11: U1.D3, R1.Pin_0
  N12: LED1.anode, R1.Pin_1
  N13: LED2.anode, R2.Pin_1

custom parts:
  RFID-RC522-v3: A simple China made RFID-RC522 Reader (6x4 cm); do check the pin labels, as this is a MFRC522 based clone.
  YwRobot Breadboard Power Supply: The YwRobot Breadboard Power Supply (MB-V2) has two power rails; they can be 5V or 3V3. Power to the module can be provided through the female USB socket or through the A10 (female) 2.1mm power jack.
  NodeMCU V1.0: ESP8266 based NodeMCU
